# Fritzing sketch Circuit (saved by Fritzing 1.0.3b)
perfboards: 1

parts:
  M2 = Stepper Motor - Bipolar
  M3 = Stepper Motor - Bipolar
  M4 = Stepper Motor - Bipolar
  Part1 = Arduino Mega 2560 (Rev3)
  JACK1 = 2.1mm Barrel Jack with Terminal Block
  M1 = Stepper Motor - Bipolar
  L2 = Solenoid
  L3 = Solenoid
  L5 = Solenoid
  L6 = Solenoid
  L7 = Solenoid
  L8 = Solenoid
  RY1 = SSR-40VA
  RY2 = SSR-40VA
  RY3 = SSR-40VA
  RY4 = SSR-40VA
  RY5 = SSR-40VA
  RY6 = SSR-40VA
  RY7 = SSR-40VA
  RY8 = SSR-40VA
  JACK2 = 2.1mm Barrel Jack with Terminal Block
  L4 = Solenoid
  L1 = Solenoid
  JL012-13-5_1 = JL012-13-5.2 Lever (Limit) Switch SPDT + NO + NC [part_number=JL012-13-5.2]
  M5 = 1 chan 5v relay module
  RY9 = SSR-40VA
  Dot_Matrix1 = LED Dot Matrix 32x32 or 64x32
  A5 = Teensy 4.1
  R1 = Resistor [tolerance=±5% power=0.25W resistance=10000 package=THT]
  R2 = Resistor [tolerance=±5% power=0.25W resistance=20000 package=THT]
  A6 = TB6600 NEMA-17-23 STEPPER MOTOR DRIVER [package=THT]
  A7 = TB6600 NEMA-17-23 STEPPER MOTOR DRIVER [package=THT]
  A8 = TB6600 NEMA-17-23 STEPPER MOTOR DRIVER [package=THT]
  A9 = TB6600 NEMA-17-23 STEPPER MOTOR DRIVER [package=THT]

nets:
  N1: M2.A, A7.Pin_6
  N2: M2.C, A7.Pin_5
  N3: M2.B, A7.Pin_4
  N4: M2.D, A7.Pin_3
  N5: M3.A, A8.Pin_6
  N6: M3.C, A8.Pin_5
  N7: M3.B, A8.Pin_4
  N8: M3.D, A8.Pin_3
  N9: M4.A, A9.Pin_6
  N10: M4.C, A9.Pin_5
  N11: M4.B, A9.Pin_4
  N12: M4.D, A9.Pin_3
  GND: Part1.GND, M5.pin_2, RY9.Pin_4, Dot_Matrix1.GND, A5.Pin_38, A5.Pin_50, A5.Pin_63, R2.Pin_1, A9.Pin_12
  N13: Part1.D8_PWM, R1.Pin_0
  N14: Part1.5V, M5.pin_1
  N15: Part1.D22, RY8.Pin_3
  N16: Part1.D23, RY4.Pin_3
  N17: Part1.D24, RY3.Pin_3
  N18: Part1.D25, RY5.Pin_3
  N19: Part1.D26, RY2.Pin_3
  N20: Part1.D27, RY6.Pin_3
  N21: Part1.D28, RY1.Pin_3
  N22: Part1.D29, RY7.Pin_3
  N23: Part1.D42, A6.Pin_9
  N24: Part1.D43, A6.Pin_7
  N25: Part1.D44, A7.Pin_9
  N26: Part1.D45, A7.Pin_7
  N27: Part1.D46, A8.Pin_9
  N28: Part1.D47, A8.Pin_7
  N29: Part1.D48, A9.Pin_7
  N30: Part1.D49, A9.Pin_9
  N31: JACK1.POS, RY9.Pin_1
  N32: JACK1.NEG, A6.Pin_2, A7.Pin_2, A8.Pin_2, A9.Pin_2
  N33: M1.A, A6.Pin_6
  N34: M1.C, A6.Pin_5
  N35: M1.B, A6.Pin_4
  N36: M1.D, A6.Pin_3
  N37: L2.pin1, L3.pin1, L5.pin1, L6.pin1, L7.pin1, L8.pin1, JACK2.NEG, L4.pin1, L1.pin1, JL012-13-5_1.NO
  N38: L2.pin2, RY4.Pin_2
  N39: L3.pin2, RY6.Pin_2
  N40: L5.pin2, RY5.Pin_2
  N41: L6.pin2, RY3.Pin_2
  N42: L7.pin2, RY7.Pin_2
  N43: L8.pin2, RY8.Pin_2
  N44: RY1.Pin_1, RY2.Pin_1, RY3.Pin_1, RY4.Pin_1, RY5.Pin_1, RY6.Pin_1, RY7.Pin_1, RY8.Pin_1, M5.pin_4
  N45: RY1.Pin_2, L1.pin2
  N46: RY1.Pin_4, RY2.Pin_4, RY3.Pin_4, RY4.Pin_4, RY5.Pin_4, RY6.Pin_4, RY7.Pin_4, RY8.Pin_4
  N47: RY2.Pin_2, L4.pin2
  N48: JACK2.POS, M5.pin_6
  N49: JL012-13-5_1.C, M5.pin_3, RY9.Pin_3
  N50: RY9.Pin_2, A6.Pin_1, A7.Pin_1, A8.Pin_1, A9.Pin_1
  N51: Dot_Matrix1.G1, A5.Pin_16
  N52: Dot_Matrix1.G2, A5.Pin_19
  N53: Dot_Matrix1.B, A5.Pin_22
  N54: Dot_Matrix1.D, A5.Pin_24
  N55: Dot_Matrix1.LAT, A5.Pin_53
  N56: Dot_Matrix1.R1, A5.Pin_15
  N57: Dot_Matrix1.B1, A5.Pin_17
  N58: Dot_Matrix1.R2, A5.Pin_18
  N59: Dot_Matrix1.B2, A5.Pin_20
  N60: Dot_Matrix1.A, A5.Pin_21
  N61: Dot_Matrix1.C, A5.Pin_23
  N62: Dot_Matrix1.CLK, A5.Pin_55
  N63: Dot_Matrix1.OE, A5.Pin_54
  N64: A5.Pin_42, R1.Pin_1, R2.Pin_0
  N65: A6.Pin_8, A6.Pin_10, A6.Pin_11, A6.Pin_12, A7.Pin_8, A7.Pin_10, A7.Pin_11, A7.Pin_12, A8.Pin_8, A8.Pin_10, A8.Pin_11, A8.Pin_12, A9.Pin_8, A9.Pin_10, A9.Pin_11

notes:
  Top solenoids
  Bottom solenoids
  24v
  12V

custom parts:
  SSR-40VA: SSR-40VA solid state relay.
  JL012-13-5.2 Lever (Limit) Switch SPDT + NO + NC: Micro Switch; Model No.: JL012-13.5-2; Actuator Action: Momentary; Actuator Type: Hinge Lever; Contact Configuration: 1NO, 1NC (SPDT) Temperature -25~65℃；Relative humidity: below 85%; Rate Voltage: 125V AC; Rated Current: 1A.
  1 chan 5v relay module: 1 Channel 5V Relay Module Board Shield with Optocoupler Support High and Low Level Trigger for Arduino.
  LED Dot Matrix 32x32 or 64x32: P3, P5 indoor matrix without controller
  Teensy 4.1: The Teensy is a complete USB-based microcontoller development system, in a very small footprint, capable of implementing many types of projects. All programming is done via the USB port. No special programmer is needed, only a standard micro-USB cable and a PC or Macintosh with a USB port.
  TB6600 NEMA-17-23 STEPPER MOTOR DRIVER: cheap Nema-17-23 steppermotor driver board
